// Logisim project 4BitRippleCounter.circ as structural Verilog: 1 circuit, main circuit main
module main (
  output [3:0] Up_Counter,
  output [3:0] Down_Counter
);

  wire clock_1_out;

  T_Flip_Flop #(.trigger("falling")) A (
    .clk(Up_Counter[2]), .T(1'b1), .Q(Up_Counter[3]), .Qn(Down_Counter[3]));  // open: preset, reset, en
  T_Flip_Flop #(.trigger("falling")) B (
    .clk(Up_Counter[1]), .T(1'b1), .Q(Up_Counter[2]), .Qn(Down_Counter[2]));  // open: preset, reset, en
  T_Flip_Flop #(.trigger("falling")) C (
    .clk(Up_Counter[0]), .T(1'b1), .Q(Up_Counter[1]), .Qn(Down_Counter[1]));  // open: preset, reset, en
  T_Flip_Flop #(.trigger("falling")) D (
    .clk(clock_1_out), .T(1'b1), .Q(Up_Counter[0]), .Qn(Down_Counter[0]));  // open: preset, reset, en
  Clock clock_1 (.out(clock_1_out));

  // Notes on the sheet:
  //   4 bit UP & DOWN Ripple Counter
endmodule
