// Logisim project 4bit Universal Shift Register.circ as structural Verilog: 1 circuit, main circuit main
module main (
  input  in_1,
  input  [1:0] in_2,
  input  in_3,
  input  in_4,
  input  in_5,
  input  in_6
);

  wire A_q, B_q, C_q, clock_1_out, D_q, multiplexer_1_out, multiplexer_2_out, multiplexer_3_out,
       multiplexer_4_out, Serial_Left_Input_out, Serial_Right_Input_out;

  Shift_Register #(.length(4), .trigger("falling")) Serial_Right_Input (.out(Serial_Right_Input_out));  // open: shift, in, clk, load, clr, d0, q0, d1, q1, d2, q2, d3, q3
  Clock clock_1 (.out(clock_1_out));
  Multiplexer #(.select(2)) multiplexer_1 (
    .in0(A_q), .in1(Serial_Right_Input_out), .in2(B_q), .in3(in_3), .out(multiplexer_1_out), .sel(in_2));  // open: en
  D_Flip_Flop #(.trigger("falling")) A (
    .clk(clock_1_out), .D(multiplexer_1_out), .Q(A_q), .reset(in_1));  // open: Qn, preset, en
  Multiplexer #(.select(2)) multiplexer_2 (
    .in0(B_q), .in1(A_q), .in2(C_q), .in3(in_4), .out(multiplexer_2_out), .sel(in_2));  // open: en
  D_Flip_Flop #(.trigger("falling")) B (
    .clk(clock_1_out), .D(multiplexer_2_out), .Q(B_q), .reset(in_1));  // open: Qn, preset, en
  Multiplexer #(.select(2)) multiplexer_3 (
    .in0(C_q), .in1(B_q), .in2(D_q), .in3(in_5), .out(multiplexer_3_out), .sel(in_2));  // open: en
  D_Flip_Flop #(.trigger("falling")) C (
    .clk(clock_1_out), .D(multiplexer_3_out), .Q(C_q), .reset(in_1));  // open: Qn, preset, en
  Multiplexer #(.select(2)) multiplexer_4 (
    .in0(D_q), .in1(C_q), .in2(Serial_Left_Input_out), .in3(in_6), .out(multiplexer_4_out), .sel(in_2));  // open: en
  D_Flip_Flop #(.trigger("falling")) D (
    .clk(clock_1_out), .D(multiplexer_4_out), .Q(D_q), .reset(in_1));  // open: Qn, preset, en
  Shift_Register #(.length(4), .trigger("falling")) Serial_Left_Input (.out(Serial_Left_Input_out));  // open: shift, in, clk, load, clr, d0, q0, d1, q1, d2, q2, d3, q3

  // Notes on the sheet:
  //   00 - No Change
  //   01 - Right Shift
  //   10- Left Shift
  //   11 - Parallel Load
endmodule
