// Logisim project BCDCounter.circ as structural Verilog: 1 circuit, main circuit main
module main (
  output [3:0] out_1
);

  wire and_1_out, clock_1_out, not_1_out, not_2_out;

  T_Flip_Flop #(.trigger("falling")) t_ff_1 (
    .clk(out_1[2]), .T(1'b1), .Q(out_1[3]), .reset(and_1_out));  // open: Qn, preset, en
  not not_1 (not_1_out, out_1[2]);
  T_Flip_Flop #(.trigger("falling")) t_ff_2 (
    .clk(out_1[1]), .T(1'b1), .Q(out_1[2]), .reset(and_1_out));  // open: Qn, preset, en
  not not_2 (not_2_out, out_1[0]);
  T_Flip_Flop #(.trigger("falling")) t_ff_3 (
    .clk(out_1[0]), .T(1'b1), .Q(out_1[1]), .reset(and_1_out));  // open: Qn, preset, en
  and and_1 (and_1_out, out_1[3], not_1_out, out_1[1], not_2_out);
  T_Flip_Flop #(.trigger("falling")) t_ff_4 (
    .clk(clock_1_out), .T(1'b1), .Q(out_1[0]), .reset(and_1_out));  // open: Qn, preset, en
  Clock clock_1 (.out(clock_1_out));
endmodule
