// Logisim project Binary to BCD XS-3.circ as structural Verilog: 1 circuit, main circuit main
module main (
  input  in_1,
  input  [3:0] in_2,
  input  [3:0] in_3,
  input  in_4,
  input  in_5,
  input  in_6,
  input  [3:0] in_7,
  input  [3:0] in_8,
  output [3:0] bcd_output,
  output C,
  output [3:0] out_11,
  output out_12,
  output out_13,
  output out_14
);

  wire adder_1_cout, and_1_out, and_2_out;
  wire [3:0] adder_1_out, adder_2_out;

  Adder #(.width(4)) adder_1 (.a(in_2), .b(in_3), .out(adder_1_out), .cin(in_1), .cout(adder_1_cout));
  Adder #(.width(4)) adder_2 (.a(in_7), .b(in_8), .out(adder_2_out), .cin(in_6), .cout(out_12));
  and and_1 (and_1_out, adder_1_out[2], adder_1_out[3]);
  and and_2 (and_2_out, adder_1_out[3], adder_1_out[1]);
  not not_1 (out_13, out_12);
  or or_1 (C, and_1_out, and_2_out, adder_1_cout);
  Adder #(.width(4)) adder_3 (.a(adder_2_out), .b({{2{out_13}}, out_12, 1'b1}), .out(out_11));  // open: cin, cout
  Adder #(.width(4)) adder_4 (.a(adder_1_out), .b({in_5, {2{C}}, in_4}), .out(bcd_output));  // open: cin, cout

  assign out_14 = out_13;

  // Notes on the sheet:
  //   K
  //   K
  //   z1
  //   z2
  //   z4
  //   z8
  //   BINARY TO BCD USING TWO PARALLEL ADDERS
  //   BINARY TO EXCESS-3 USING TWO PARALLEL ADDERS
  //   z1
  //   z2
  //   z4
  //   z8
  //   s1
  //   s2
  //   s4
  //   s8
  //   excess-3 output
endmodule
