// Logisim project RepeatingSequence.circ as structural Verilog: 1 circuit, main circuit main
module main (
  input  in_1,
  output [1:0] out_2
);

  wire and_1_out, and_2_out, B_qn, C_q, clock_1_out, or_1_out;

  Clock clock_1 (.out(clock_1_out));
  and and_1 (and_1_out, C_q, or_1_out);
  T_Flip_Flop #(.trigger("falling")) C (.clk(clock_1_out), .T(1'b1), .Q(C_q), .reset(in_1));  // open: Qn, preset, en
  or or_1 (or_1_out, out_2[0], out_2[1]);
  T_Flip_Flop #(.trigger("falling")) B (
    .clk(clock_1_out), .T(and_1_out), .Q(out_2[1]), .Qn(B_qn), .reset(in_1));  // open: preset, en
  and and_2 (and_2_out, B_qn, C_q);
  T_Flip_Flop #(.trigger("falling")) A (
    .clk(clock_1_out), .T(and_2_out), .Q(out_2[0]), .reset(in_1));  // open: Qn, preset, en

  // Notes on the sheet:
  //   Sequence Generated: 0,0,1,1,2,2,0,0....
  //   MSB to be ignored
endmodule
