// Logisim project Ring and Johnson Counter.circ as structural Verilog: 1 circuit, main circuit main
module main (
  input  in_1,
  input  in_2
);

  wire clock_1_out, clock_2_out, d_ff_1_q, d_ff_2_q, d_ff_3_q, d_ff_4_q, d_ff_5_q, d_ff_6_q, d_ff_7_q,
       d_ff_8_q, d_ff_8_qn;

  Clock clock_1 (.out(clock_1_out));
  LED led_1 (.in(d_ff_1_q));
  Clock clock_2 (.out(clock_2_out));
  D_Flip_Flop d_ff_1 (.clk(clock_1_out), .D(d_ff_7_q), .Q(d_ff_1_q), .preset(in_1));  // open: Qn, en, reset
  LED led_2 (.in(d_ff_2_q));
  D_Flip_Flop d_ff_2 (.clk(clock_2_out), .D(d_ff_8_qn), .Q(d_ff_2_q), .reset(in_2));  // open: Qn, preset, en
  LED led_3 (.in(d_ff_3_q));
  D_Flip_Flop d_ff_3 (.clk(clock_1_out), .D(d_ff_1_q), .Q(d_ff_3_q), .reset(in_1));  // open: Qn, preset, en
  LED led_4 (.in(d_ff_4_q));
  D_Flip_Flop d_ff_4 (.clk(clock_2_out), .D(d_ff_2_q), .Q(d_ff_4_q), .reset(in_2));  // open: Qn, preset, en
  LED led_5 (.in(d_ff_5_q));
  D_Flip_Flop d_ff_5 (.clk(clock_1_out), .D(d_ff_3_q), .Q(d_ff_5_q), .reset(in_1));  // open: Qn, preset, en
  LED led_6 (.in(d_ff_7_q));
  LED led_7 (.in(d_ff_6_q));
  D_Flip_Flop d_ff_6 (.clk(clock_2_out), .D(d_ff_4_q), .Q(d_ff_6_q), .reset(in_2));  // open: Qn, preset, en
  D_Flip_Flop d_ff_7 (.clk(clock_1_out), .D(d_ff_5_q), .Q(d_ff_7_q), .reset(in_1));  // open: Qn, preset, en
  LED led_8 (.in(d_ff_8_q));
  D_Flip_Flop d_ff_8 (.clk(clock_2_out), .D(d_ff_6_q), .Q(d_ff_8_q), .Qn(d_ff_8_qn), .reset(in_2));  // open: preset, en

  // Notes on the sheet:
  //   Ring Counter 
  //   Johnson Counter
endmodule
