// Logisim project Ripple Counter.circ as structural Verilog: 1 circuit, main circuit main
module main (
  output [3:0] out_1
);

  wire clock_1_out;

  T_Flip_Flop #(.trigger("falling")) A (.clk(out_1[2]), .T(1'b1), .Q(out_1[3]));  // open: Qn, preset, reset, en
  T_Flip_Flop #(.trigger("falling")) B (.clk(out_1[1]), .T(1'b1), .Q(out_1[2]));  // open: Qn, preset, reset, en
  T_Flip_Flop #(.trigger("falling")) C (.clk(out_1[0]), .T(1'b1), .Q(out_1[1]));  // open: Qn, preset, reset, en
  T_Flip_Flop D (.clk(clock_1_out), .T(1'b1), .Q(out_1[0]));  // open: Qn, preset, reset, en
  Clock clock_1 (.out(clock_1_out));
endmodule
