// Logisim project Universal shift register.circ as structural Verilog: 1 circuit, main circuit main
module main (
  input  [1:0] in_1,
  input  in_2,
  input  in_3,
  input  in_4,
  output [7:0] out_5
);

  wire clock_1_out, multiplexer_1_out, multiplexer_2_out, multiplexer_3_out, multiplexer_4_out,
       multiplexer_5_out, multiplexer_6_out, multiplexer_7_out, multiplexer_8_out;

  Clock clock_1 (.out(clock_1_out));
  D_Flip_Flop d_ff_1 (.clk(clock_1_out), .D(multiplexer_1_out), .Q(out_5[7]));  // open: Qn, preset, en, reset
  Multiplexer #(.select(2)) multiplexer_1 (
    .in0(in_2), .in1(out_5[6]), .in2(in_3), .in3(out_5[7]), .out(multiplexer_1_out), .sel(in_1));  // open: en
  D_Flip_Flop d_ff_2 (.clk(clock_1_out), .D(multiplexer_2_out), .Q(out_5[6]));  // open: Qn, preset, en, reset
  Multiplexer #(.select(2)) multiplexer_2 (
    .in0(in_2), .in1(out_5[5]), .in2(out_5[7]), .in3(out_5[6]), .out(multiplexer_2_out), .sel(in_1));  // open: en
  D_Flip_Flop d_ff_3 (.clk(clock_1_out), .D(multiplexer_3_out), .Q(out_5[5]));  // open: Qn, preset, en, reset
  Multiplexer #(.select(2)) multiplexer_3 (
    .in0(in_2), .in1(out_5[4]), .in2(out_5[6]), .in3(out_5[5]), .out(multiplexer_3_out), .sel(in_1));  // open: en
  Multiplexer #(.select(2)) multiplexer_4 (
    .in0(in_2), .in1(out_5[3]), .in2(out_5[5]), .in3(out_5[4]), .out(multiplexer_4_out), .sel(in_1));  // open: en
  D_Flip_Flop d_ff_4 (.clk(clock_1_out), .D(multiplexer_4_out), .Q(out_5[4]));  // open: Qn, preset, en, reset
  D_Flip_Flop d_ff_5 (.clk(clock_1_out), .D(multiplexer_5_out), .Q(out_5[3]));  // open: Qn, preset, en, reset
  Multiplexer #(.select(2)) multiplexer_5 (
    .in0(in_2), .in1(out_5[2]), .in2(out_5[4]), .in3(out_5[3]), .out(multiplexer_5_out), .sel(in_1));  // open: en
  Multiplexer #(.select(2)) multiplexer_6 (
    .in0(in_2), .in1(out_5[1]), .in2(out_5[3]), .in3(out_5[2]), .out(multiplexer_6_out), .sel(in_1));  // open: en
  D_Flip_Flop d_ff_6 (.clk(clock_1_out), .D(multiplexer_6_out), .Q(out_5[2]));  // open: Qn, preset, en, reset
  Multiplexer #(.select(2)) multiplexer_7 (
    .in0(in_2), .in1(out_5[1]), .in2(out_5[2]), .in3(out_5[1]), .out(multiplexer_7_out), .sel(in_1));  // open: en
  D_Flip_Flop d_ff_7 (.clk(clock_1_out), .D(multiplexer_7_out), .Q(out_5[1]));  // open: Qn, preset, en, reset
  Multiplexer #(.select(2)) multiplexer_8 (
    .in0(in_2), .in1(in_4), .in2(out_5[1]), .in3(out_5[1]), .out(multiplexer_8_out), .sel(in_1));  // open: en
  D_Flip_Flop d_ff_8 (.clk(clock_1_out), .D(multiplexer_8_out), .Q(out_5[1]));  // open: Qn, preset, en, reset

  assign out_5[0] = out_5[1];

  // Notes on the sheet:
  //   Right Input Stream
  //   Left Input Stream
endmodule
