// Logisim project Vending Machine.circ as structural Verilog: 1 circuit, main circuit main
module main (
  input  Nicket,
  input  Dime,
  input  Reset_Button
);

  wire and_1_out, and_2_out, and_3_out, and_4_out, and_5_out, and_6_out, and_7_out, clock_1_out, d_ff_1_q,
       d_ff_2_q, not_1_out, not_2_out, not_3_out, not_4_out, or_1_out, or_2_out;

  and and_1 (and_1_out, d_ff_2_q, Nicket);
  not not_1 (not_1_out, Nicket);
  and and_2 (and_2_out, Nicket, not_4_out);
  and and_3 (and_3_out, d_ff_1_q, not_1_out);
  or or_1 (or_1_out, and_1_out, and_3_out, and_2_out, and_4_out);
  not not_2 (not_2_out, Dime);
  and and_4 (and_4_out, Dime, d_ff_2_q);
  and and_5 (and_5_out, Dime, d_ff_2_q);
  not not_3 (not_3_out, d_ff_2_q);
  and and_6 (and_6_out, Nicket, d_ff_1_q);
  or or_2 (or_2_out, and_5_out, and_6_out);
  not not_4 (not_4_out, d_ff_1_q);
  D_Flip_Flop #(.trigger("falling")) d_ff_1 (
    .clk(clock_1_out), .D(or_2_out), .Q(d_ff_1_q), .reset(Reset_Button));  // open: Qn, preset, en
  D_Flip_Flop #(.trigger("falling")) d_ff_2 (
    .clk(clock_1_out), .D(or_1_out), .Q(d_ff_2_q), .reset(Reset_Button));  // open: Qn, preset, en
  Clock clock_1 (.out(clock_1_out));
  and and_7 (and_7_out, d_ff_1_q, d_ff_2_q);
  LED led_1 (.in(and_7_out));

  // Notes on the sheet:
  //   Q1
  //   Q0
endmodule
